// Logisim project ALU.circ as structural Verilog: 6 circuits, main circuit ALU
module ALU (
);

  wire [2:0] undriven_2;
  wire [15:0] demultiplexer_1_out0, demultiplexer_1_out1, demultiplexer_1_out2, demultiplexer_1_out3,
       demultiplexer_1_out4, demultiplexer_1_out5, demultiplexer_1_out6, demultiplexer_1_out7, undriven;

  Demultiplexer #(.select(3), .width(16)) demultiplexer_1 (
    .out0(demultiplexer_1_out0), .out1(demultiplexer_1_out1), .out2(demultiplexer_1_out2),
    .out3(demultiplexer_1_out3), .out4(demultiplexer_1_out4), .out5(demultiplexer_1_out5),
    .out6(demultiplexer_1_out6), .out7(demultiplexer_1_out7), .in(undriven), .sel(undriven_2), .en(1'b1));
endmodule

module _16_Bit_adder (
  input  [15:0] Input_a,
  input  Subtract,
  input  [15:0] Input_b,
  output [15:0] Sum
);

  wire n4_bit_adder_1_carry_out, n4_bit_adder_2_carry_out, n4_bit_adder_3_carry_out;

  _4_Bit_adder u_4_bit_adder_1 (
    .Input_a(Input_a[11:8]), .Input_b(Input_b[11:8]), .Sum(Sum[11:8]), .Carry_out(n4_bit_adder_1_carry_out),
    .Carry_in(n4_bit_adder_2_carry_out));
  _4_Bit_adder u_4_bit_adder_2 (
    .Input_a(Input_a[15:12]), .Input_b(Input_b[15:12]), .Sum(Sum[15:12]),
    .Carry_out(n4_bit_adder_2_carry_out), .Carry_in(Subtract));
  _4_Bit_adder u_4_bit_adder_3 (
    .Input_a(Input_a[7:4]), .Input_b(Input_b[7:4]), .Sum(Sum[7:4]), .Carry_out(n4_bit_adder_3_carry_out),
    .Carry_in(n4_bit_adder_1_carry_out));
  // _4_Bit_adder 4_bit_adder_4: pin names not known; wires that end beside it: Subtract, Input_a[3:0], Input_b[3:0], n4_bit_adder_3_carry_out, Sum[3:0], Subtract
endmodule

module _4_Bit_adder_subtractor (
  input  [3:0] B,
  input  [3:0] A,
  input  Subtract,
  output [3:0] Out,
  output Sign
);

  wire n4_bit_adder_1_carry_out, not_1_out;
  wire [0:0] and_1_out;
  wire [3:0] n4_bit_adder_1_sum, xor_1_out, xor_6_out;

  xor xor_1 (xor_1_out[0], B[0], Subtract);
  xor xor_2 (xor_1_out[1], B[1], Subtract);
  xor xor_3 (xor_1_out[2], B[2], Subtract);
  xor xor_4 (xor_1_out[3], B[3], Subtract);
  _4_Bit_adder u_4_bit_adder_1 (
    .Input_a(A), .Input_b(xor_1_out), .Sum(n4_bit_adder_1_sum), .Carry_out(n4_bit_adder_1_carry_out),
    .Carry_in(Subtract));
  not not_1 (not_1_out, n4_bit_adder_1_carry_out);
  and and_1 (and_1_out[0], not_1_out, Subtract);
  xor xor_5 (Sign, n4_bit_adder_1_carry_out, Subtract);
  xor xor_6 (xor_6_out[0], n4_bit_adder_1_sum[0], and_1_out[0]);
  xor xor_7 (xor_6_out[1], n4_bit_adder_1_sum[1], and_1_out[0]);
  xor xor_8 (xor_6_out[2], n4_bit_adder_1_sum[2], and_1_out[0]);
  xor xor_9 (xor_6_out[3], n4_bit_adder_1_sum[3], and_1_out[0]);
  _4_Bit_adder u_4_bit_adder_2 (
    .Input_a({3'b000, and_1_out[0]}), .Input_b(xor_6_out), .Sum(Out), .Carry_in(1'b0));  // open: Carry_out
endmodule

module _4_Bit_adder (
  input  [3:0] Input_a,
  input  Carry_in,
  input  [3:0] Input_b,
  output [3:0] Sum,
  output Carry_out
);

  wire full_adder_1_carry_out, full_adder_2_carry_out, full_adder_3_carry_out;

  Full_adder full_adder_1 (
    .Input_a(Input_a[1]), .Input_b(Input_b[1]), .Carry_in(full_adder_2_carry_out), .Sum(Sum[1]),
    .Carry_out(full_adder_1_carry_out));
  Full_adder full_adder_2 (
    .Input_a(Input_a[0]), .Input_b(Input_b[0]), .Carry_in(Carry_in), .Sum(Sum[0]),
    .Carry_out(full_adder_2_carry_out));
  Full_adder full_adder_3 (
    .Input_a(Input_a[2]), .Input_b(Input_b[2]), .Carry_in(full_adder_1_carry_out), .Sum(Sum[2]),
    .Carry_out(full_adder_3_carry_out));
  Full_adder full_adder_4 (
    .Input_a(Input_a[3]), .Input_b(Input_b[3]), .Carry_in(full_adder_3_carry_out), .Sum(Sum[3]),
    .Carry_out(Carry_out));
endmodule

module Full_adder (
  input  Input_a,
  input  Input_b,
  input  Carry_in,
  output Sum,
  output Carry_out
);

  wire half_adder_1_carry, half_adder_1_sum, half_adder_2_carry;

  Half_adder half_adder_1 (.Input_a(Input_a), .Input_b(Input_b), .Sum(half_adder_1_sum), .Carry(half_adder_1_carry));
  Half_adder half_adder_2 (.Input_a(half_adder_1_sum), .Input_b(Carry_in), .Sum(Sum), .Carry(half_adder_2_carry));
  or or_1 (Carry_out, half_adder_2_carry, half_adder_1_carry);
endmodule

module Half_adder (
  input  Input_a,
  input  Input_b,
  output Sum,
  output Carry
);

  xor xor_1 (Sum, Input_a, Input_b);
  and and_1 (Carry, Input_a, Input_b);
endmodule
