// Logisim project Main bus.circ as structural Verilog: 1 circuit, main circuit Main bus
module Main_bus (
  input  in_1
);

  wire AccBuf, ALUBuf, clk, decoder_1_out2, decoder_1_out3, decoder_1_out4, decoder_1_out5, decoder_1_out7,
       IBuf, IRBuf, Jump, MARBuf, nor_1_out, not_1_out, OBuf, PCBuf, PCEn, RAMRead, RegBuf;
  wire [1:0] priority_encoder_1_out;
  wire [2:0] ALU, Phase;
  wire [15:0] Accumulator_register_q, controlled_buffer_1_out, controlled_buffer_2_out,
       controlled_buffer_4_out, controlled_buffer_6_out, controlled_buffer_7_out, controlled_buffer_8_out,
       Input_register_q, InstrData, Instruction_register_q, Memory_access_register_q, Output_register_q,
       Program_counter_q, ram_1_data, rom_1_data, undriven;

  Register #(.width(16)) Memory_access_register (
    .D(controlled_buffer_2_out), .en(1'b1), .Q(Memory_access_register_q), .clk(clk));  // open: clr
  Register #(.width(16)) Instruction_register (
    .D(controlled_buffer_4_out), .en(1'b1), .Q(Instruction_register_q), .clk(clk));  // open: clr
  Decoder #(.select(3)) decoder_1 (
    .out0(PCBuf), .out1(IRBuf), .out2(decoder_1_out2), .out3(decoder_1_out3), .out4(decoder_1_out4),
    .out5(decoder_1_out5), .out6(PCEn), .out7(decoder_1_out7), .sel(Phase), .en(1'b1));
  Priority_Encoder #(.select(2), .disabled(0)) priority_encoder_1 (
    .in0(decoder_1_out2), .in1(decoder_1_out3), .in2(decoder_1_out4), .in3(decoder_1_out5),
    .out(priority_encoder_1_out), .en_in(nor_1_out));  // open: gs, en_out
  nor nor_1 (nor_1_out, PCEn, decoder_1_out7, PCBuf, IRBuf);
  assign InstrData = {{4{1'b0}}, Instruction_register_q[11:0]};  // Bit_Extender bit_extender_1
  Clock clock_1 (.out(clk));
  Counter #(.width(16), .max('hffff)) Program_counter (
    .load(Jump), .D(InstrData), .count(PCEn), .Q(Program_counter_q), .clk(clk));  // open: carry, clr
  assign controlled_buffer_1_out = PCBuf ? Program_counter_q : 16'bz;  // Controlled_Buffer controlled_buffer_1
  assign controlled_buffer_2_out = MARBuf ? controlled_buffer_1_out : 16'bz;  // Controlled_Buffer controlled_buffer_2
  RAM #(.addrWidth(16), .dataWidth(16)) ram_1 (
    .addr(Memory_access_register_q), .data(ram_1_data), .clk(clk), .ld(1'b1));  // open: sel, clr
  assign controlled_buffer_1_out = RAMRead ? ram_1_data : 16'bz;  // Controlled_Buffer controlled_buffer_3
  assign controlled_buffer_4_out = IRBuf ? controlled_buffer_1_out : 16'bz;  // Controlled_Buffer controlled_buffer_4
  ROM #(.addrWidth(6), .dataWidth(16)) rom_1 (
    .addr({Instruction_register_q[15:12], priority_encoder_1_out}),
    .data({rom_1_data[15:11], ALU, Jump, IBuf, OBuf, AccBuf, RegBuf, ALUBuf, rom_1_data[1:0]}));  // open: sel
  Counter #(.width(3), .max('h7)) counter_1 (.count(1'b1), .Q(Phase), .clk(clk));  // open: load, D, carry, clr
  assign controlled_buffer_1_out = ALUBuf ? Accumulator_register_q : 16'bz;  // Controlled_Buffer controlled_buffer_5
  not not_1 (not_1_out, AccBuf);
  assign controlled_buffer_6_out = AccBuf ? controlled_buffer_1_out : 16'bz;  // Controlled_Buffer controlled_buffer_6
  assign controlled_buffer_7_out = RegBuf ? controlled_buffer_1_out : 16'bz;  // Controlled_Buffer controlled_buffer_7
  assign controlled_buffer_8_out = OBuf ? controlled_buffer_1_out : 16'bz;  // Controlled_Buffer controlled_buffer_8
  assign controlled_buffer_1_out = IBuf ? InstrData : 16'bz;  // Controlled_Buffer controlled_buffer_9
  assign controlled_buffer_6_out = not_1_out ? undriven : 16'bz;  // Controlled_Buffer controlled_buffer_10
  Register #(.width(16)) Input_register (
    .D(controlled_buffer_7_out), .en(1'b1), .Q(Input_register_q), .clk(clk));  // open: clr
  Register #(.width(16)) Output_register (
    .D(controlled_buffer_8_out), .Q(Output_register_q), .clk(clk));  // open: en, clr
  Register #(.width(16)) Accumulator_register (
    .D(controlled_buffer_6_out), .en(1'b1), .Q(Accumulator_register_q), .clk(clk));  // open: clr
  Hex_Digit_Display hex_digit_display_1 (.value(Output_register_q[11:8]));  // open: dp
  Hex_Digit_Display hex_digit_display_2 (.value(Output_register_q[15:12]));  // open: dp
  // ALU alu_1: pin names not known
  Hex_Digit_Display hex_digit_display_3 (.value(Output_register_q[7:4]));  // open: dp
  or or_1 (MARBuf, PCBuf, rom_1_data[0]);
  or or_2 (RAMRead, IRBuf, rom_1_data[1]);
  Hex_Digit_Display hex_digit_display_4 (.value(Output_register_q[3:0]));  // open: dp
endmodule
