// Logisim project RAM.circ as structural Verilog
module RAM (
  input  [19:0] in_1,
  input  [2:0] Input,
  input  Enable,
  input  R_W,
  output [19:0] out_5
);

  wire [7:0] n3x8_decoder_1_output;
  wire [19:0] or_1_out, or_3_out, word_1_output, word_2_output, word_3_output, word_4_output, word_5_output,
       word_6_output, word_7_output, word_8_output;

  _3x8_decoder u_3x8_decoder_1 (.Enable(Enable), .Output(n3x8_decoder_1_output), .Input(Input));
  Word word_1 (.Select(n3x8_decoder_1_output[0]), .R_W(R_W), .Data(in_1), .Output(word_1_output));
  Word word_2 (.Select(n3x8_decoder_1_output[1]), .R_W(R_W), .Data(in_1), .Output(word_2_output));
  Word word_3 (.Select(n3x8_decoder_1_output[2]), .R_W(R_W), .Data(in_1), .Output(word_3_output));
  Word word_4 (.Select(n3x8_decoder_1_output[3]), .R_W(R_W), .Data(in_1), .Output(word_4_output));
  Word word_5 (.Select(n3x8_decoder_1_output[4]), .R_W(R_W), .Data(in_1), .Output(word_5_output));
  Word word_6 (.Select(n3x8_decoder_1_output[5]), .R_W(R_W), .Data(in_1), .Output(word_6_output));
  Word word_7 (.Select(n3x8_decoder_1_output[6]), .R_W(R_W), .Data(in_1), .Output(word_7_output));
  Word word_8 (.Select(n3x8_decoder_1_output[7]), .R_W(R_W), .Data(in_1), .Output(word_8_output));
  assign or_1_out = word_8_output | word_7_output | word_6_output | word_5_output;  // OR_Gate or_1, 20 bits wide
  assign out_5 = or_1_out | or_3_out;  // OR_Gate or_2, 20 bits wide
  assign or_3_out = word_4_output | word_3_output | word_2_output | word_1_output;  // OR_Gate or_3, 20 bits wide
endmodule

module Word (
  input  [19:0] Data,
  input  Select,
  input  R_W,
  output [19:0] Output
);

  Memory_cell memory_cell_1 (.Select(Select), .Input(Data[19]), .Output(Output[19]), .R_W(R_W));
  Memory_cell memory_cell_2 (.Select(Select), .Input(Data[18]), .Output(Output[18]), .R_W(R_W));
  Memory_cell memory_cell_3 (.Select(Select), .Input(Data[17]), .Output(Output[17]), .R_W(R_W));
  Memory_cell memory_cell_4 (.Select(Select), .Input(Data[16]), .Output(Output[16]), .R_W(R_W));
  Memory_cell memory_cell_5 (.Select(Select), .Input(Data[15]), .Output(Output[15]), .R_W(R_W));
  Memory_cell memory_cell_6 (.Select(Select), .Input(Data[14]), .Output(Output[14]), .R_W(R_W));
  Memory_cell memory_cell_7 (.Select(Select), .Input(Data[13]), .Output(Output[13]), .R_W(R_W));
  Memory_cell memory_cell_8 (.Select(Select), .Input(Data[12]), .Output(Output[12]), .R_W(R_W));
  Memory_cell memory_cell_9 (.Select(Select), .Input(Data[11]), .Output(Output[11]), .R_W(R_W));
  Memory_cell memory_cell_10 (.Select(Select), .Input(Data[10]), .Output(Output[10]), .R_W(R_W));
  Memory_cell memory_cell_11 (.Select(Select), .Input(Data[9]), .Output(Output[9]), .R_W(R_W));
  Memory_cell memory_cell_12 (.Select(Select), .Input(Data[8]), .Output(Output[8]), .R_W(R_W));
  Memory_cell memory_cell_13 (.Select(Select), .Input(Data[7]), .Output(Output[7]), .R_W(R_W));
  Memory_cell memory_cell_14 (.Select(Select), .Input(Data[6]), .Output(Output[6]), .R_W(R_W));
  Memory_cell memory_cell_15 (.Select(Select), .Input(Data[5]), .Output(Output[5]), .R_W(R_W));
  Memory_cell memory_cell_16 (.Select(Select), .Input(Data[4]), .Output(Output[4]), .R_W(R_W));
  Memory_cell memory_cell_17 (.Select(Select), .Input(Data[3]), .Output(Output[3]), .R_W(R_W));
  Memory_cell memory_cell_18 (.Select(Select), .Input(Data[2]), .Output(Output[2]), .R_W(R_W));
  Memory_cell memory_cell_19 (.Select(Select), .Input(Data[1]), .Output(Output[1]), .R_W(R_W));
  Memory_cell memory_cell_20 (.Select(Select), .Input(Data[0]), .Output(Output[0]), .R_W(R_W));
endmodule

module _3x8_decoder (
  input  [2:0] Input,
  input  Enable,
  output [7:0] Output
);

  wire and_1_out, and_2_out, not_1_out;

  not not_1 (not_1_out, Input[2]);
  _2x4_decoder u_2x4_decoder_1 (
    .Input_a(Input[1]), .Input_b(Input[0]), .Output_0(Output[0]), .Output_1(Output[1]), .Output_2(Output[2]),
    .Output_3(Output[3]), .Enable(and_1_out));
  and and_1 (and_1_out, Enable, not_1_out);
  _2x4_decoder u_2x4_decoder_2 (
    .Input_a(Input[1]), .Input_b(Input[0]), .Output_0(Output[4]), .Output_1(Output[5]), .Output_2(Output[6]),
    .Output_3(Output[7]), .Enable(and_2_out));
  and and_2 (and_2_out, Enable, Input[2]);
endmodule

module _2x4_decoder (
  input  Input_a,
  input  Input_b,
  input  Enable,
  output Output_0,
  output Output_1,
  output Output_2,
  output Output_3
);

  wire not_1_out, not_2_out;

  not not_1 (not_1_out, Input_a);
  not not_2 (not_2_out, Input_b);
  and and_1 (Output_0, not_1_out, Enable, not_2_out);
  and and_2 (Output_1, not_1_out, Enable, Input_b);
  and and_3 (Output_2, Input_a, Enable, not_2_out);
  and and_4 (Output_3, Input_a, Enable, Input_b);
endmodule

module Memory_cell (
  input  Select,
  input  Input,
  input  R_W,
  output Output
);

  wire and_1_out, and_2_out, not_1_out, not_2_out, sr_latch_1_output;

  not not_1 (not_1_out, Input);
  and and_1 (and_1_out, Select, not_2_out, not_1_out);
  and and_2 (and_2_out, Select, not_2_out, Input);
  not not_2 (not_2_out, R_W);
  SR_latch sr_latch_1 (.Set(and_1_out), .Reset(and_2_out), .Output(sr_latch_1_output));
  and and_3 (Output, Select, sr_latch_1_output, R_W);
endmodule

module SR_latch (
  input  Set,
  input  Reset,
  output Output
);

  wire nor_2_out;

  nor nor_1 (Output, Set, nor_2_out);
  nor nor_2 (nor_2_out, Output, Reset);
endmodule
